// Logisim project 6502.circ as structural Verilog: 6 circuits, main circuit main
module main (
  output [7:0] out_1,
  output [7:0] out_2,
  output [7:0] out_3
);

  wire program_counter_1_p1, program_counter_1_p2;
  wire [7:0] stack_pointer_register_p1;

  // buffer_8bit buffer_8bit_1: pin names not known
  // buffer_8bit buffer_8bit_2: pin names not known
  buffer_8bit buffer_8bit_3 (.data_in(stack_pointer_register_p1), .data_out(out_1));  // open: enable_acL
  // buffer_8bit buffer_8bit_4: pin names not known; wires that end beside it: out_1
  // buffer_8bit buffer_8bit_5: pin names not known; wires that end beside it: out_1
  // register_8bit index_register_Y: pin names not known
  // register_8bit index_register_X: pin names not known
  // register_8bit stack_pointer_register: pin names not known; wires that end beside it: stack_pointer_register_p1
  // register_8bit accumulator_A: pin names not known
  // data_buffer data_buffer_1: pin names not known
  // program_counter program_counter_1: pin names not known; wires that end beside it: program_counter_1_p1, program_counter_1_p2
  // buffer_8bit buffer_8bit_6: pin names not known
  // buffer_8bit buffer_8bit_7: pin names not known
  // buffer_8bit buffer_8bit_8: pin names not known
  // buffer_8bit buffer_8bit_9: pin names not known
  // buffer_8bit buffer_8bit_10: pin names not known
  // register_8bit process_state_register: pin names not known
  // register_8bit instruction_register: pin names not known

  // Notes on the sheet:
  //   ALU
endmodule

module program_counter (
  input  output_enable_acL,
  input  load_parallel_LB_acL,
  input  reset_acL,
  input  CountEnable,
  input  [7:0] LB_Input_acH,
  input  load_parallel_HB_acL,
  input  [7:0] H_Input_acH,
  input  clk,
  output [7:0] PC_OUT_LOW_BYTE,
  output [7:0] PC_OUT_HIGH_BYTE
);

  wire n7408_1_pin4, n7408_1_pin5, n74163_1_pin7, n74163_1_pin15, n74163_2_pin7;

  _74163 u_74163_1 (
    .pin1(reset_acL), .pin2(clk), .pin3(LB_Input_acH[4]), .pin4(LB_Input_acH[5]), .pin5(LB_Input_acH[6]),
    .pin6(LB_Input_acH[7]), .pin7(n74163_1_pin7), .pin15(n74163_1_pin15), .pin14(PC_OUT_LOW_BYTE[4]),
    .pin13(PC_OUT_LOW_BYTE[5]), .pin12(PC_OUT_LOW_BYTE[6]), .pin11(PC_OUT_LOW_BYTE[7]), .pin10(CountEnable),
    .pin9(load_parallel_LB_acL));
  _74163 u_74163_2 (
    .pin1(reset_acL), .pin2(clk), .pin3(H_Input_acH[4]), .pin4(H_Input_acH[5]), .pin5(H_Input_acH[6]),
    .pin6(H_Input_acH[7]), .pin7(n74163_2_pin7), .pin14(PC_OUT_HIGH_BYTE[4]), .pin13(PC_OUT_HIGH_BYTE[5]),
    .pin12(PC_OUT_HIGH_BYTE[6]), .pin11(PC_OUT_HIGH_BYTE[7]), .pin10(CountEnable), .pin9(load_parallel_HB_acL));  // open: pin15
  _74163 u_74163_3 (
    .pin1(reset_acL), .pin2(clk), .pin3(LB_Input_acH[0]), .pin4(LB_Input_acH[1]), .pin5(LB_Input_acH[2]),
    .pin6(LB_Input_acH[3]), .pin7(CountEnable), .pin15(n74163_1_pin7), .pin14(PC_OUT_LOW_BYTE[0]),
    .pin13(PC_OUT_LOW_BYTE[1]), .pin12(PC_OUT_LOW_BYTE[2]), .pin11(PC_OUT_LOW_BYTE[3]), .pin10(CountEnable),
    .pin9(load_parallel_LB_acL));
  _7408 u_7408_1 (
    .pin4(n7408_1_pin4), .pin5(n7408_1_pin5), .pin6(n74163_2_pin7), .pin13(n74163_1_pin7),
    .pin12(n74163_1_pin15), .pin11(n7408_1_pin5));  // open: pin1, pin2, pin3, pin10, pin9, pin8
  _74163 u_74163_4 (
    .pin1(reset_acL), .pin2(clk), .pin3(H_Input_acH[0]), .pin4(H_Input_acH[1]), .pin5(H_Input_acH[2]),
    .pin6(H_Input_acH[3]), .pin7(n7408_1_pin5), .pin15(n7408_1_pin4), .pin14(PC_OUT_HIGH_BYTE[0]),
    .pin13(PC_OUT_HIGH_BYTE[1]), .pin12(PC_OUT_HIGH_BYTE[2]), .pin11(PC_OUT_HIGH_BYTE[3]),
    .pin10(CountEnable), .pin9(load_parallel_HB_acL));

  // Notes on the sheet:
  //   LB
  //   UB
endmodule

module register_8bit (
  input  load_enable_acL,
  input  [7:0] Input_byte,
  input  clk,
  output [7:0] output_byte
);

  ttl_74194 ttl_74194_1 (
    .d1(Input_byte[1]), .d0(Input_byte[0]), .d2(Input_byte[2]), .d3(Input_byte[3]), .cp(clk),
    .in_6(load_enable_acL), .q0(output_byte[0]), .q1(output_byte[1]), .q2(output_byte[2]), .q3(output_byte[3]));
  ttl_74194 ttl_74194_2 (
    .d1(Input_byte[5]), .d0(Input_byte[4]), .d2(Input_byte[6]), .d3(Input_byte[7]), .cp(clk),
    .in_6(load_enable_acL), .q0(output_byte[4]), .q1(output_byte[5]), .q2(output_byte[6]), .q3(output_byte[7]));
endmodule

module ttl_74194 (
  input  d0,
  input  d1,
  input  d2,
  input  d3,
  input  cp,
  input  in_6,
  output q0,
  output q1,
  output q2,
  output q3
);

  wire not_1_out;

  not not_1 (not_1_out, in_6);
  Register #(.width(4)) register_1 (.D({d3, d2, d1, d0}), .en(not_1_out), .clk(cp), .Q({q3, q2, q1, q0}));  // open: clr
endmodule

module data_buffer (
  input  enable_acL,
  input  [7:0] data_in,
  output [7:0] data_out
);

  _74125 u_74125_1 (
    .pin1(enable_acL), .pin2(data_in[1]), .pin3(data_out[1]), .pin4(enable_acL), .pin5(data_in[0]),
    .pin6(data_out[0]), .pin13(enable_acL), .pin12(data_in[2]), .pin11(data_out[2]), .pin10(enable_acL),
    .pin9(data_in[3]), .pin8(data_out[3]));
  _74125 u_74125_2 (
    .pin1(enable_acL), .pin2(data_in[5]), .pin3(data_out[5]), .pin4(enable_acL), .pin5(data_in[4]),
    .pin6(data_out[4]), .pin13(enable_acL), .pin12(data_in[6]), .pin11(data_out[6]), .pin10(enable_acL),
    .pin9(data_in[7]), .pin8(data_out[7]));
endmodule

module buffer_8bit (
  input  enable_acL,
  input  [7:0] data_in,
  output [7:0] data_out
);

  _74125 u_74125_1 (
    .pin1(enable_acL), .pin2(data_in[1]), .pin3(data_out[1]), .pin4(enable_acL), .pin5(data_in[0]),
    .pin6(data_out[0]), .pin13(enable_acL), .pin12(data_in[2]), .pin11(data_out[2]), .pin10(enable_acL),
    .pin9(data_in[3]), .pin8(data_out[3]));
  _74125 u_74125_2 (
    .pin1(enable_acL), .pin2(data_in[5]), .pin3(data_out[5]), .pin4(enable_acL), .pin5(data_in[4]),
    .pin6(data_out[4]), .pin13(enable_acL), .pin12(data_in[6]), .pin11(data_out[6]), .pin10(enable_acL),
    .pin9(data_in[7]), .pin8(data_out[7]));
endmodule
